# Fritzing sketch Guvercinsavar_seması (saved by Fritzing 0.8.7b)
breadboards: 1

parts:
  Eleman1 = Arduino Uno (Rev3) - ICSP
  J1 = Piezo Speaker
  LED1 = LED - 5mm [color="Red (633nm)" package="5 mm [THT]"]
  J2 = Basic Servo
  Eleman2 = HC-SR501 Body Sensor Module
  R1 = Resistor [package="2010 [SMD]"]

nets:
  VCC: Eleman1.5V, J2.vcc, Eleman2.VCC
  GND: Eleman1.GND, J1.pin1, LED1.cathode, J2.gnd, Eleman2.GND
  N1: Eleman1.D8, Eleman2.OUT
  N2: Eleman1.D9_PWM, J2.pulse
  N3: Eleman1.D2, R1.Pin_1
  N4: Eleman1.D3_PWM, J1.pin2
  N5: LED1.anode, R1.Pin_0

custom parts:
  HC-SR501 Body Sensor Module: Pyroelectric Infrared PIR Motion Sensor Detector Module
